// Logisim project control-logic.circ as structural Verilog: 1 circuit, main circuit control_logic
module control_logic (
  input  [31:0] Instruction,
  input  BrEq,
  input  BrLt,
  output PCSel,
  output RegWEn,
  output [2:0] ImmSel,
  output BrUn,
  output ASel,
  output BSel,
  output [3:0] ALUSel,
  output MemWEn,
  output [1:0] WBSel
);

  wire and_37_out, and_38_out, and_39_out, and_40_out, funct3_0, funct3_1, funct3_2, funct3_3, funct3_4,
       funct3_5, funct3_6, funct3_7, funct7_0, funct7_1, funct7_32, is_add, is_addi, is_and, is_andi,
       is_auipc, is_beq, is_bge, is_bgeu, is_blt, is_bltu, is_bne, is_Btype, is_Itype, is_jal, is_jalr,
       is_lb, is_lh, is_load, is_lui, is_lw, is_mul, is_mulh, is_mulhu, is_or, is_ori, is_Rtype, is_sb,
       is_sh, is_sll, is_slli, is_slt, is_slti, is_sra, is_srai, is_srl, is_srli, is_Stype, is_sub, is_sw,
       is_xor, is_xori, Itype_funct3_5, not_1_out, not_2_out, or_1_out, or_2_out, or_3_out, or_4_out,
       or_5_out, or_7_out, Rtype_funct3_0, Rtype_funct3_1, Rtype_funct3_5;
  wire [5:0] priority_encoder_1_out;
  wire [15:14] rom_1_data;

  Comparator #(.mode("unsigned"), .width(3)) comparator_1 (
    .a(Instruction[14:12]), .b(3'b110), .gt(funct3_7), .eq(funct3_6));  // open: lt
  Comparator #(.mode("unsigned"), .width(3)) comparator_2 (
    .a(Instruction[14:12]), .b(3'b101), .eq(funct3_5));  // open: gt, lt
  Comparator #(.mode("unsigned"), .width(3)) comparator_3 (
    .a(Instruction[14:12]), .b(3'b100), .eq(funct3_4));  // open: gt, lt
  Comparator #(.mode("unsigned"), .width(3)) comparator_4 (
    .a(Instruction[14:12]), .b(3'b011), .eq(funct3_3));  // open: gt, lt
  Comparator #(.mode("unsigned"), .width(3)) comparator_5 (
    .a(Instruction[14:12]), .b(3'b010), .eq(funct3_2));  // open: gt, lt
  Comparator #(.mode("unsigned"), .width(3)) comparator_6 (
    .a(Instruction[14:12]), .b(3'b001), .eq(funct3_1), .lt(funct3_0));  // open: gt
  and and_1 (Rtype_funct3_0, is_Rtype, funct3_0);
  and and_2 (Rtype_funct3_1, is_Rtype, funct3_1);
  and and_3 (is_slt, is_Rtype, funct3_2);
  and and_4 (is_mulhu, is_Rtype, funct3_3);
  and and_5 (is_add, Rtype_funct3_0, funct7_0);
  and and_6 (is_mul, Rtype_funct3_0, funct7_1);
  and and_7 (is_sub, Rtype_funct3_0, funct7_32);
  and and_8 (is_beq, is_Btype, funct3_0);
  and and_9 (is_bne, is_Btype, funct3_1);
  and and_10 (is_blt, is_Btype, funct3_4);
  and and_11 (is_bge, is_Btype, funct3_5);
  and and_12 (is_addi, is_Itype, funct3_0);
  and and_13 (is_slli, is_Itype, funct3_1);
  and and_14 (is_slti, is_Itype, funct3_2);
  and and_15 (is_sb, is_Stype, funct3_0);
  and and_16 (is_lb, is_load, funct3_0);
  Comparator #(.mode("unsigned"), .width(7)) comparator_7 (
    .a(Instruction[6:0]), .b(7'b1100011), .eq(is_Btype));  // open: gt, lt
  Comparator #(.mode("unsigned"), .width(7)) comparator_8 (
    .a(Instruction[6:0]), .b(7'b0110011), .eq(is_Rtype));  // open: gt, lt
  Comparator #(.mode("unsigned"), .width(7)) comparator_9 (
    .a(Instruction[6:0]), .b(7'b0100011), .eq(is_Stype));  // open: gt, lt
  Comparator #(.mode("unsigned"), .width(7)) comparator_10 (
    .a(Instruction[6:0]), .b(7'b1101111), .eq(is_jal));  // open: gt, lt
  Comparator #(.mode("unsigned"), .width(7)) comparator_11 (
    .a(Instruction[6:0]), .b(7'b0110111), .eq(is_lui));  // open: gt, lt
  Comparator #(.mode("unsigned"), .width(7)) comparator_12 (
    .a(Instruction[31:25]), .b(7'b0000001), .eq(funct7_1), .lt(funct7_0));  // open: gt
  Comparator #(.mode("unsigned"), .width(7)) comparator_13 (
    .a(Instruction[31:25]), .b(7'b0100000), .eq(funct7_32));  // open: gt, lt
  and and_17 (is_srl, Rtype_funct3_5, funct7_0);
  and and_18 (is_sra, Rtype_funct3_5, funct7_32);
  and and_19 (is_bltu, is_Btype, funct3_6);
  and and_20 (is_bgeu, is_Btype, funct3_7);
  and and_21 (is_xori, is_Itype, funct3_4);
  and and_22 (Itype_funct3_5, is_Itype, funct3_5);
  and and_23 (is_ori, is_Itype, funct3_6);
  and and_24 (is_andi, is_Itype, funct3_7);
  and and_25 (is_xor, is_Rtype, funct3_4);
  and and_26 (Rtype_funct3_5, is_Rtype, funct3_5);
  and and_27 (is_or, is_Rtype, funct3_6);
  and and_28 (is_and, is_Rtype, funct3_7);
  Priority_Encoder #(.select_enc(6)) priority_encoder_1 (
    .in0(is_add), .in1(is_mul), .in2(is_sub), .in3(is_sll), .in4(is_mulh), .in5(is_mulhu), .in6(is_slt),
    .in7(is_xor), .in8(is_srl), .in9(is_sra), .in10(is_or), .in11(is_and), .in12(is_lb), .in13(is_lh),
    .in14(is_lw), .in15(is_addi), .in16(is_slli), .in17(is_slti), .in18(is_xori), .in19(is_srli),
    .in20(is_srai), .in21(is_ori), .in22(is_andi), .in23(is_sb), .in24(is_sh), .in25(is_sw), .in26(is_beq),
    .in27(is_bne), .in28(is_blt), .in29(is_bge), .in30(is_bltu), .in31(is_bgeu), .in32(is_auipc),
    .in33(is_lui), .in34(is_jal), .in35(is_jalr), .out(priority_encoder_1_out));  // open: in36, in37, in38, in39, in40, in41, in42, in43, in44, in45, in46, in47, in48, in49, in50, in51, in52, in53, in54, in55, in56, in57, in58, in59, in60, in61, in62, in63, gs, en_out, en_in
  Comparator #(.mode("unsigned"), .width(7)) comparator_14 (
    .a(Instruction[6:0]), .b(7'b0000011), .eq(is_load));  // open: gt, lt
  Comparator #(.mode("unsigned"), .width(7)) comparator_15 (
    .a(Instruction[6:0]), .b(7'b1100111), .eq(is_jalr));  // open: gt, lt
  Comparator #(.mode("unsigned"), .width(7)) comparator_16 (
    .a(Instruction[6:0]), .b(7'b0010011), .eq(is_Itype));  // open: gt, lt
  Comparator #(.mode("unsigned"), .width(7)) comparator_17 (
    .a(Instruction[6:0]), .b(7'b0010111), .eq(is_auipc));  // open: gt, lt
  and and_29 (is_sh, is_Stype, funct3_1);
  and and_30 (is_lh, is_load, funct3_1);
  ROM #(.addrWidth(6), .dataWidth(16)) rom_1 (
    .addr(priority_encoder_1_out),
    .data({rom_1_data, WBSel, MemWEn, ALUSel, BSel, ASel, BrUn, ImmSel, RegWEn}));
  and and_31 (is_sll, Rtype_funct3_1, funct7_0);
  and and_32 (is_mulh, Rtype_funct3_1, funct7_1);
  and and_33 (is_srli, Itype_funct3_5, funct7_0);
  and and_34 (is_srai, Itype_funct3_5, funct7_32);
  and and_35 (is_sw, is_Stype, funct3_2);
  and and_36 (is_lw, is_load, funct3_2);
  not not_1 (not_1_out, BrEq);
  not not_2 (not_2_out, BrLt);
  and and_37 (and_37_out, is_beq, BrEq);
  and and_38 (and_38_out, is_bne, not_1_out);
  or or_1 (or_1_out, is_blt, is_bltu);
  or or_2 (or_2_out, is_bge, is_bgeu);
  and and_39 (and_39_out, or_1_out, BrLt);
  and and_40 (and_40_out, or_2_out, not_2_out);
  or or_3 (or_3_out, and_37_out, and_38_out);
  or or_4 (or_4_out, and_39_out, and_40_out);
  or or_5 (or_5_out, is_jalr, is_jal);
  or or_6 (PCSel, or_5_out, or_7_out);
  or or_7 (or_7_out, or_3_out, or_4_out);

  // Other names for the same wires on the sheet: opcode[6:0] = Instruction[6:0]; rd_imm[4:0] = Instruction[11:7];
  //   funct3[2:0] = Instruction[14:12]; rs1_rs2[9:0] = Instruction[24:15]; funct7[6:0] = Instruction[31:25]

  // Notes on the sheet:
  //   R TYPE
  //   S TYPE
  //   B TYPE
  //   LOAD TYPE
  //   I TYPE
  //   INPUTS to your circuit
  //   DON'T CHANGE THE LOCATIONS OF THE INPUTS AND OUTPUTS!
  //   Connect ROM Input here ->
  //   OUTPUT from your circuit
  //   contents of rom_1 (hex, n*v repeats v):
  //   102b 142b 162b 10ab 14ab 15ab 112b 122b 12ab 16ab 132b 13ab 61 61 61 1061 10e1 1161 1261 12e1 16e1
  //   1361 13e1 862 862 862 4*44 54 44 1047 17e7 2049 2061
  //   ROM FOR CONTROL LOGIC
  //   This is only if you choose to do the ROM option
  //   CONNECT
  //   WIRE
  //   TO
  //   USE
  //   ROM
  //   Reminder: If using ROM, use combinational logic for PCSel
endmodule
