// Logisim project cpu.circ as structural Verilog: 1 circuit, main circuit cpu
module cpu (
  input  clk,
  input  [31:0] Instruction,
  input  [31:0] MemReadData,
  output [31:0] MemAddress,
  output [31:0] ProgramCounter,
  output [31:0] ra,
  output [31:0] sp,
  output [31:0] t0,
  output [31:0] t1,
  output [31:0] t2,
  output [31:0] s0,
  output [31:0] s1,
  output [31:0] a0,
  output [3:0] MemWriteMask,
  output [31:0] MemWriteData
);

  wire ASel, BrEq, BrLt, BrUn, BSel, MemWEn, PCSel, RegWEn;
  wire [1:0] WBSel;
  wire [2:0] funct3, ImmSel;
  wire [3:0] ALUSel;
  wire [11:0] func7;
  wire [19:0] NewInstruction;
  wire [31:0] DataToReg, Immediate, multiplexer_2_out, multiplexer_3_out, NewProgramCounter, PCplus4,
       PCplus4WB, ReadData1, ReadData2, RegWriteData;

  Multiplexer #(.width(32)) multiplexer_1 (.in0(PCplus4), .in1(MemAddress), .out(ProgramCounter), .sel(PCSel));
  Register #(.width(32)) PC (.D(ProgramCounter), .en(1'b1), .clk(clk), .Q(NewProgramCounter));  // open: clr
  Adder #(.width(32)) adder_1 (.a(ProgramCounter), .b(32'h4), .out(PCplus4));  // open: cin, cout
  Adder #(.width(32)) adder_2 (.a(NewProgramCounter), .b(32'h4), .out(PCplus4WB));  // open: cin, cout
  Register #(.width(32)) register_1 (
    .D(Instruction), .en(1'b1), .clk(clk), .Q({func7, NewInstruction[19:15], funct3, NewInstruction[11:0]}));  // open: clr
  control_logic control_logic_1 (
    .Instruction({func7, NewInstruction[19:15], funct3, NewInstruction[11:0]}), .BrEq(BrEq), .BrLt(BrLt),
    .PCSel(PCSel), .RegWEn(RegWEn), .ImmSel(ImmSel), .BrUn(BrUn), .ASel(ASel), .BSel(BSel), .ALUSel(ALUSel),
    .MemWEn(MemWEn), .WBSel(WBSel));
  regfile regfile_1 (
    .ReadIndex1(NewInstruction[19:15]), .ReadIndex2(func7[4:0]), .WriteIndex(NewInstruction[11:7]),
    .WriteData(RegWriteData), .RegWEn(RegWEn), .clk(clk), .ra(ra), .sp(sp), .t0(t0), .t1(t1), .t2(t2),
    .s0(s0), .s1(s1), .a0(a0), .ReadData1(ReadData1), .ReadData2(ReadData2));
  imm_gen imm_gen_1 (
    .Instruction({func7, NewInstruction[19:15], funct3, NewInstruction[11:0]}), .ImmSel(ImmSel),
    .Immediate(Immediate));
  Multiplexer #(.width(32)) multiplexer_2 (.in0(ReadData2), .in1(Immediate), .out(multiplexer_2_out), .sel(BSel));
  Multiplexer #(.width(32)) multiplexer_3 (
    .in0(NewProgramCounter), .in1(ReadData1), .out(multiplexer_3_out), .sel(ASel));
  alu alu_1 (.A(multiplexer_3_out), .B(multiplexer_2_out), .ALUSel(ALUSel), .ALUResult(MemAddress));
  branch_comp branch_comp_1 (.BrData1(ReadData1), .BrData2(ReadData2), .BrUn(BrUn), .BrEq(BrEq), .BrLt(BrLt));
  Multiplexer #(.select(2), .width(32)) multiplexer_4 (
    .in0(DataToReg), .in1(MemAddress), .in2(PCplus4WB), .out(RegWriteData), .sel(WBSel));  // open: in3
  partial_store partial_store_1 (
    .Instruction({func7, NewInstruction[19:15], funct3, NewInstruction[11:0]}), .MemAddress(MemAddress),
    .DataFromReg(ReadData2), .MemWEn(MemWEn), .MemWriteMask(MemWriteMask), .DataToMem(MemWriteData));
  partial_load partial_load_1 (
    .Instruction({func7, NewInstruction[19:15], funct3, NewInstruction[11:0]}), .MemAddress(MemAddress),
    .DataFromMem(MemReadData), .DataToReg(DataToReg));

  // Other names for the same wires on the sheet: opcode[6:0] = NewInstruction[6:0]; rd[4:0] = NewInstruction[11:7];
  //   NewInstruction (some bits) = {func7, funct3}; rs1[4:0] = NewInstruction[19:15]; rs2[4:0] = func7[4:0]

  // Notes on the sheet:
  //   From ALU
  //   From Adder ^
  //   pipeline register here
  //   To IMEM
  //   IMEM (do **NOT** move this)
  //   register here
  //   From IMEM
  //   Inputs/Outputs for testing. Do **NOT** move these.
  //   It is OK to move the PC, RegFile, ALU, MEM, Branch Comp, Imm Gen, Partial Load, Partial Store and Control Logic to wherever is most convenient for you when constructing your CPU, and to delete this text
  //   To DMEM
  //   DMEM (do **NOT** move this)
  //   From DMEM
endmodule
